// Digital circuit 4-bit-Registar.dig as structural Verilog
module _4_bit_Registar (
  input  [3:0] Data,
  input  C,
  output [3:0] Q
);

  D_FF d_ff_1 (.D(Data[0]), .C(C), .Q(Q[0]));  // open: nQ
  D_FF d_ff_2 (.D(Data[1]), .C(C), .Q(Q[1]));  // open: nQ
  D_FF d_ff_3 (.D(Data[2]), .C(C), .Q(Q[2]));  // open: nQ
  D_FF d_ff_4 (.D(Data[3]), .C(C), .Q(Q[3]));  // open: nQ
endmodule
