// Digital circuit GPR.dig as structural Verilog
module GPR (
  input  [1:0] Address,
  input  [3:0] Data,
  input  [1:0] Control,
  input  clk,
  output [3:0] out
);

  wire and_1_out, and_2_out, and_3_out, and_4_out, decoder_1_out_0, decoder_1_out_1, decoder_1_out_2,
       decoder_1_out_3;
  wire [3:0] gpr1_1_out, gpr1_2_out, gpr1_3_out, gpr1_4_out;

  Decoder #(.Selector_Bits(2)) decoder_1 (
    .sel(Address), .out_0(decoder_1_out_0), .out_1(decoder_1_out_1), .out_2(decoder_1_out_2),
    .out_3(decoder_1_out_3));
  and and_1 (and_1_out, decoder_1_out_0, clk);
  and and_2 (and_2_out, decoder_1_out_1, clk);
  and and_3 (and_3_out, decoder_1_out_2, clk);
  and and_4 (and_4_out, decoder_1_out_3, clk);
  GPR1 gpr1_1 (.Clock(and_1_out), .Data(Data), .Control(Control), .Out(gpr1_1_out));
  GPR1 gpr1_2 (.Clock(and_2_out), .Data(Data), .Control(Control), .Out(gpr1_2_out));
  GPR1 gpr1_3 (.Clock(and_3_out), .Data(Data), .Control(Control), .Out(gpr1_3_out));
  GPR1 gpr1_4 (.Clock(and_4_out), .Data(Data), .Control(Control), .Out(gpr1_4_out));
  Multiplexer #(.Selector_Bits(2), .Bits(4)) multiplexer_1 (
    .sel(Address), .in_0(gpr1_1_out), .in_1(gpr1_2_out), .in_2(gpr1_3_out), .in_3(gpr1_4_out), .out(out));
endmodule
