// Digital circuit GPR1.dig as structural Verilog
module GPR1 (
  input  Clock,
  input  [3:0] Data,
  input  [1:0] Control,
  output [3:0] Out
);

  wire [3:0] multiplexer_1_out;

  Multiplexer #(.Selector_Bits(2), .Bits(4)) multiplexer_1 (
    .sel(Control), .in_0(4'b0000), .in_1(Out), .in_2(Data), .in_3(4'b0001), .out(multiplexer_1_out));
  D_FF d_ff_1 (.D(multiplexer_1_out[3]), .C(Clock), .Q(Out[3]));  // open: nQ
  D_FF d_ff_2 (.D(multiplexer_1_out[2]), .C(Clock), .Q(Out[2]));  // open: nQ
  D_FF d_ff_3 (.D(multiplexer_1_out[1]), .C(Clock), .Q(Out[1]));  // open: nQ
  D_FF d_ff_4 (.D(multiplexer_1_out[0]), .C(Clock), .Q(Out[0]));  // open: nQ

  // Notes on the sheet:
  //   Control: 0 = clear
  //   1 = load
  //   2 = store
  //   3 = store 1
endmodule
