// Digital circuit dram.dig as structural Verilog
module dram (
  input  [3:0] Address_bits,
  input  Clock,
  input  [3:0] data,
  input  [1:0] control,
  output [3:0] \output 
);

  wire and_1_out, and_2_out, and_3_out, and_4_out, and_5_out, and_6_out, and_7_out, and_8_out, and_9_out,
       and_10_out, and_11_out, and_12_out, and_13_out, and_14_out, and_15_out, and_16_out, decoder_1_out_0,
       decoder_1_out_1, decoder_1_out_2, decoder_1_out_3, decoder_1_out_4, decoder_1_out_5, decoder_1_out_6,
       decoder_1_out_7, decoder_1_out_8, decoder_1_out_9, decoder_1_out_10, decoder_1_out_11,
       decoder_1_out_12, decoder_1_out_13, decoder_1_out_14, decoder_1_out_15;
  wire [3:0] _4_bit_register2_1_p4, _4_bit_register2_2_p4, _4_bit_register2_3_p4, _4_bit_register2_4_p4,
       _4_bit_register2_5_p4, _4_bit_register2_6_p4, _4_bit_register2_7_p4, _4_bit_register2_8_p4,
       _4_bit_register2_9_p4, _4_bit_register2_10_p4, _4_bit_register2_11_p4, _4_bit_register2_12_p4,
       _4_bit_register2_13_p4, _4_bit_register2_14_p4, _4_bit_register2_15_p4;

  Decoder #(.Selector_Bits(4)) decoder_1 (
    .sel(Address_bits), .out_0(decoder_1_out_0), .out_1(decoder_1_out_1), .out_2(decoder_1_out_2),
    .out_3(decoder_1_out_3), .out_4(decoder_1_out_4), .out_5(decoder_1_out_5), .out_6(decoder_1_out_6),
    .out_7(decoder_1_out_7), .out_8(decoder_1_out_8), .out_9(decoder_1_out_9), .out_10(decoder_1_out_10),
    .out_11(decoder_1_out_11), .out_12(decoder_1_out_12), .out_13(decoder_1_out_13),
    .out_14(decoder_1_out_14), .out_15(decoder_1_out_15));
  and and_1 (and_1_out, decoder_1_out_0, Clock);
  and and_2 (and_2_out, decoder_1_out_4, Clock);
  and and_3 (and_3_out, decoder_1_out_8, Clock);
  and and_4 (and_4_out, decoder_1_out_12, Clock);
  // _4_bit_register2 _4_bit_register2_1: pin names not known; wires that end beside it: and_1_out, data, control, _4_bit_register2_1_p4
  // _4_bit_register2 _4_bit_register2_2: pin names not known; wires that end beside it: and_2_out, data, control, _4_bit_register2_2_p4
  // _4_bit_register2 _4_bit_register2_3: pin names not known; wires that end beside it: and_3_out, data, control, _4_bit_register2_3_p4
  // _4_bit_register2 _4_bit_register2_4: pin names not known; wires that end beside it: and_4_out, data, control, _4_bit_register2_4_p4
  and and_5 (and_5_out, decoder_1_out_1, Clock);
  and and_6 (and_6_out, decoder_1_out_5, Clock);
  and and_7 (and_7_out, decoder_1_out_9, Clock);
  and and_8 (and_8_out, decoder_1_out_13, Clock);
  // _4_bit_register2 _4_bit_register2_5: pin names not known; wires that end beside it: and_5_out, data, control, _4_bit_register2_5_p4
  // _4_bit_register2 _4_bit_register2_6: pin names not known; wires that end beside it: and_6_out, data, control, _4_bit_register2_6_p4
  // _4_bit_register2 _4_bit_register2_7: pin names not known; wires that end beside it: and_7_out, data, control, _4_bit_register2_7_p4
  // _4_bit_register2 _4_bit_register2_8: pin names not known; wires that end beside it: and_8_out, data, control, _4_bit_register2_8_p4
  and and_9 (and_9_out, decoder_1_out_2, Clock);
  and and_10 (and_10_out, decoder_1_out_6, Clock);
  and and_11 (and_11_out, decoder_1_out_10, Clock);
  and and_12 (and_12_out, decoder_1_out_14, Clock);
  // _4_bit_register2 _4_bit_register2_9: pin names not known; wires that end beside it: and_9_out, data, control, _4_bit_register2_9_p4
  // _4_bit_register2 _4_bit_register2_10: pin names not known; wires that end beside it: and_10_out, data, control, _4_bit_register2_10_p4
  // _4_bit_register2 _4_bit_register2_11: pin names not known; wires that end beside it: and_11_out, data, control, _4_bit_register2_11_p4
  // _4_bit_register2 _4_bit_register2_12: pin names not known; wires that end beside it: and_12_out, data, control, _4_bit_register2_12_p4
  and and_13 (and_13_out, decoder_1_out_3, Clock);
  and and_14 (and_14_out, decoder_1_out_7, Clock);
  and and_15 (and_15_out, decoder_1_out_11, Clock);
  and and_16 (and_16_out, Clock, decoder_1_out_15);
  // _4_bit_register2 _4_bit_register2_13: pin names not known; wires that end beside it: and_13_out, data, control, _4_bit_register2_13_p4
  // _4_bit_register2 _4_bit_register2_14: pin names not known; wires that end beside it: and_14_out, data, control, _4_bit_register2_14_p4
  // _4_bit_register2 _4_bit_register2_15: pin names not known; wires that end beside it: and_15_out, data, control, _4_bit_register2_15_p4
  // _4_bit_register2 _4_bit_register2_16: pin names not known; wires that end beside it: and_16_out, data, control, _4_bit_register2_4_p4
  Multiplexer #(.Selector_Bits(4), .Bits(4)) multiplexer_1 (
    .sel(Address_bits), .in_0(_4_bit_register2_1_p4), .in_1(_4_bit_register2_5_p4),
    .in_2(_4_bit_register2_9_p4), .in_3(_4_bit_register2_13_p4), .in_4(_4_bit_register2_2_p4),
    .in_5(_4_bit_register2_6_p4), .in_6(_4_bit_register2_10_p4), .in_7(_4_bit_register2_14_p4),
    .in_8(_4_bit_register2_3_p4), .in_9(_4_bit_register2_7_p4), .in_10(_4_bit_register2_11_p4),
    .in_11(_4_bit_register2_15_p4), .in_12(_4_bit_register2_4_p4), .in_13(_4_bit_register2_8_p4),
    .in_14(_4_bit_register2_12_p4), .in_15(_4_bit_register2_4_p4), .out(\output ));
endmodule
