// Digital circuit General_registar.dig as structural Verilog
module General_registar (
  input  [1:0] store,
  input  clk,
  input  [3:0] data,
  input  clear,
  input  [1:0] load,
  output [3:0] out
);

  wire and_5_out, and_6_out, and_7_out, and_8_out, decoder_1_out_0, decoder_1_out_1, decoder_1_out_2,
       decoder_1_out_3, not_1_out, or_1_out, or_2_out, or_3_out, or_4_out;
  wire [3:0] and_1_out, r0_q, R1_q, r2_q, r3_q;

  Decoder #(.Selector_Bits(2)) decoder_1 (
    .sel(store), .out_0(decoder_1_out_0), .out_1(decoder_1_out_1), .out_2(decoder_1_out_2),
    .out_3(decoder_1_out_3));
  or or_1 (or_1_out, decoder_1_out_0, clear);
  or or_2 (or_2_out, decoder_1_out_1, clear);
  or or_3 (or_3_out, decoder_1_out_2, clear);
  or or_4 (or_4_out, decoder_1_out_3, clear);
  not not_1 (not_1_out, clear);
  and and_1 (and_1_out[0], data[0], not_1_out);
  and and_2 (and_1_out[1], data[1], not_1_out);
  and and_3 (and_1_out[2], data[2], not_1_out);
  and and_4 (and_1_out[3], data[3], not_1_out);
  and and_5 (and_5_out, or_1_out, clk);
  and and_6 (and_6_out, or_2_out, clk);
  and and_7 (and_7_out, or_3_out, clk);
  and and_8 (and_8_out, or_4_out, clk);
  _4_bit_Registar r0 (.Data(and_1_out), .C(and_5_out), .Q(r0_q));
  _4_bit_Registar R1 (.Data(and_1_out), .C(and_6_out), .Q(R1_q));
  _4_bit_Registar r2 (.Data(and_1_out), .C(and_7_out), .Q(r2_q));
  _4_bit_Registar r3 (.Data(and_1_out), .C(and_8_out), .Q(r3_q));
  Multiplexer #(.Selector_Bits(2), .Bits(4)) multiplexer_1 (
    .sel(load), .in_0(r0_q), .in_1(R1_q), .in_2(r2_q), .in_3(r3_q), .out(out));
endmodule
