// Digital circuit 110-detector.dig as structural Verilog
module _110_detector (
  input  i,
  input  clk,
  output out_3
);

  wire and_1_out, and_2_out, not_1_out, or_1_out, s0_nq, s0_q, s1_nq, s1_q;

  not not_1 (not_1_out, i);
  and and_1 (and_1_out, s0_nq, i, s1_q);
  and and_2 (and_2_out, not_1_out, s1_nq, s0_q);
  or or_1 (or_1_out, and_1_out, and_2_out);
  D_FF s0 (.D(or_1_out), .C(clk), .Q(s0_q), .nQ(s0_nq));
  D_FF s1 (.D(s1_nq), .C(clk), .Q(s1_q), .nQ(s1_nq));
  and and_3 (out_3, s0_q, not_1_out, s1_nq);
endmodule
