// Digital circuit up-down-counter.dig as structural Verilog
module up_down_counter (
  input  i,
  input  clk,
  output [1:0] out_2
);

  wire and_1_out, and_2_out, and_3_out, and_4_out, and_5_out, and_6_out, not_1_out, or_1_out, or_2_out,
       s0_nq, s1_nq;

  not not_1 (not_1_out, i);
  and and_1 (and_1_out, out_2[0], i, s0_nq);
  and and_2 (and_2_out, s1_nq, s0_nq, not_1_out);
  and and_3 (and_3_out, out_2[1], not_1_out, out_2[0]);
  and and_4 (and_4_out, i, s1_nq, out_2[1]);
  and and_5 (and_5_out, s0_nq, s1_nq);
  and and_6 (and_6_out, s1_nq, out_2[1]);
  or or_1 (or_1_out, and_1_out, and_2_out, and_3_out, and_4_out);
  or or_2 (or_2_out, and_5_out, and_6_out);
  D_FF s0 (.D(or_1_out), .C(clk), .Q(out_2[1]), .nQ(s0_nq));
  D_FF s1 (.D(or_2_out), .C(clk), .Q(out_2[0]), .nQ(s1_nq));
endmodule
