// Digital circuit S-R_Flip_Flop.dig as structural Verilog
module S_R_Flip_Flop (
  input  in_1,
  input  in_2,
  input  clk,
  output Q,
  output Q_2
);

  wire nand_1_out, nand_2_out;

  nand nand_1 (nand_1_out, in_1, clk);
  nand nand_2 (nand_2_out, clk, in_2);
  nand nand_3 (Q, nand_1_out, Q_2);
  nand nand_4 (Q_2, Q, nand_2_out);
endmodule
