// Digital circuit and_or_adder.dig as structural Verilog
module and_or_adder (
  input  A,
  input  B,
  input  C,
  output sum,
  output carry_out
);

  wire and_1_out, and_2_out, and_3_out, and_4_out, and_5_out, and_6_out, and_7_out, not_1_out, not_2_out,
       not_3_out;

  not not_1 (not_1_out, A);
  not not_2 (not_2_out, B);
  not not_3 (not_3_out, C);
  and and_1 (and_1_out, not_1_out, not_2_out, C);
  and and_2 (and_2_out, not_1_out, B, not_3_out);
  and and_3 (and_3_out, A, B, C);
  and and_4 (and_4_out, A, B);
  and and_5 (and_5_out, A, not_2_out, not_3_out);
  and and_6 (and_6_out, not_1_out, B, C);
  and and_7 (and_7_out, A, not_2_out, C);
  or or_1 (sum, and_1_out, and_2_out, and_5_out, and_3_out);
  or or_2 (carry_out, and_4_out, and_6_out, and_7_out);
endmodule
