// Digital circuit hw1_full_adder.dig as structural Verilog
module hw1_full_adder (
  input  [3:0] A,
  input  [3:0] B,
  input  add_subtract,
  output Cout,
  output [3:0] Sum
);

  wire hw1_adder_1_cout, hw1_adder_2_cout, hw1_adder_3_cout, xor_1_out, xor_2_out, xor_3_out, xor_4_out;

  xor xor_1 (xor_1_out, add_subtract, B[0]);
  hw1_adder hw1_adder_1 (.A(A[0]), .B(xor_1_out), .Cin(add_subtract), .Sum(Sum[0]), .Cout(hw1_adder_1_cout));
  xor xor_2 (xor_2_out, add_subtract, B[1]);
  hw1_adder hw1_adder_2 (.A(A[1]), .B(xor_2_out), .Cin(hw1_adder_1_cout), .Sum(Sum[1]), .Cout(hw1_adder_2_cout));
  xor xor_3 (xor_3_out, add_subtract, B[2]);
  hw1_adder hw1_adder_3 (.A(A[2]), .B(xor_3_out), .Cin(hw1_adder_2_cout), .Sum(Sum[2]), .Cout(hw1_adder_3_cout));
  xor xor_4 (xor_4_out, add_subtract, B[3]);
  hw1_adder hw1_adder_4 (.A(A[3]), .B(xor_4_out), .Cin(hw1_adder_3_cout), .Sum(Sum[3]), .Cout(Cout));
endmodule
