// Digital circuit hw1_multiplier.dig as structural Verilog
module hw1_multiplier (
  input  A1,
  input  A0,
  input  B1,
  input  B0,
  output [3:0] out
);

  wire and_2_out, and_3_out, and_5_out, and_6_out, and_7_out, and_8_out, not_1_out, not_2_out, not_3_out,
       not_4_out;

  and and_1 (out[3], A1, A0, B1, B0);
  not not_1 (not_1_out, A0);
  not not_2 (not_2_out, B0);
  not not_3 (not_3_out, B1);
  and and_2 (and_2_out, A1, not_1_out, B1);
  and and_3 (and_3_out, B1, not_2_out, A1);
  not not_4 (not_4_out, A1);
  or or_1 (out[2], and_2_out, and_3_out);
  and and_4 (out[0], A1, B0);
  and and_5 (and_5_out, not_4_out, A0, B1);
  and and_6 (and_6_out, A1, not_3_out, B0);
  and and_7 (and_7_out, A1, A0, B1, not_2_out);
  and and_8 (and_8_out, A1, not_1_out, B1, B0);
  or or_2 (out[1], and_5_out, and_6_out, and_7_out, and_8_out);
endmodule
