// Digital circuit sequential_1.dig as structural Verilog
module sequential_1 (
  input  clk,
  input  i,
  output s0,
  output s1
);

  wire and_1_out, and_2_out, and_3_out, and_4_out, D0_q, D1_q, not_1_out, or_1_out, or_2_out;

  not not_1 (not_1_out, i);
  and and_1 (and_1_out, not_1_out, s1);
  and and_2 (and_2_out, s0, not_1_out);
  D_FF D1 (.D(or_2_out), .C(clk), .Q(D1_q), .nQ(s1));
  and and_3 (and_3_out, D1_q, D0_q, i);
  D_FF D0 (.D(or_1_out), .C(clk), .Q(D0_q), .nQ(s0));
  and and_4 (and_4_out, i, s0);
  or or_1 (or_1_out, and_2_out, and_3_out);
  or or_2 (or_2_out, and_4_out, and_1_out);
endmodule
