// Digital circuit sequential_2.dig as structural Verilog
module sequential_2 (
  input  i,
  input  clk,
  output \output ,
  output [1:0] state
);

  wire and_1_out, and_2_out, and_3_out, and_4_out, and_5_out, D0_nq, D1_nq, not_1_out, or_1_out, or_2_out;

  not not_1 (not_1_out, i);
  and and_1 (and_1_out, state[1], not_1_out);
  and and_2 (and_2_out, state[1], D0_nq);
  and and_3 (and_3_out, i, state[0], D1_nq);
  or or_1 (or_1_out, and_1_out, and_2_out, and_3_out);
  and and_4 (and_4_out, i, D0_nq);
  and and_5 (and_5_out, not_1_out, state[0]);
  or or_2 (or_2_out, and_4_out, and_5_out);
  D_FF D1 (.D(or_1_out), .C(clk), .Q(state[1]), .nQ(D1_nq));
  D_FF D0 (.D(or_2_out), .C(clk), .Q(state[0]), .nQ(D0_nq));
  and and_6 (\output , state[1], state[0], i);
endmodule
