// Digital circuit state_machine_1.dig as structural Verilog
module state_machine_1 (
  input  isJ,
  input  aluDone,
  input  wba,
  input  pca,
  input  idd,
  input  dmr,
  input  imr,
  input  isr,
  input  isLW,
  input  isSW,
  input  isBEQ,
  input  dma,
  input  clk,
  output Q3,
  output Q2,
  output Q1,
  output Q0
);

  wire and_1_out, and_2_out, and_3_out, and_4_out, and_5_out, and_6_out, and_7_out, and_8_out, and_9_out,
       and_10_out, and_11_out, D0_nq, D1_nq, D2_nq, D3_nq, or_1_out, or_2_out, or_3_out, or_4_out, or_5_out,
       or_6_out;

  and and_1 (and_1_out, idd, Q0, isJ, D1_nq);
  and and_2 (and_2_out, D0_nq, Q1, aluDone);
  or or_1 (or_1_out, and_1_out, and_2_out);
  and and_3 (and_3_out, isBEQ, idd);
  and and_4 (and_4_out, aluDone, isLW);
  or or_2 (or_2_out, isLW, isSW, isBEQ, isr);
  and and_5 (and_5_out, aluDone, isSW);
  or or_3 (or_3_out, isSW, isLW);
  or or_4 (or_4_out, and_5_out, and_4_out, and_3_out, dmr);
  and and_6 (and_6_out, D1_nq, Q0, idd, or_2_out);
  and and_7 (and_7_out, Q1, Q0, isSW, aluDone);
  and and_8 (and_8_out, idd, or_3_out);
  and and_9 (and_9_out, idd, isBEQ);
  and and_10 (and_10_out, Q0, aluDone, Q1);
  or or_5 (or_5_out, and_6_out, and_7_out);
  and and_11 (and_11_out, imr, D3_nq, D0_nq, D2_nq, D1_nq);
  or or_6 (or_6_out, and_11_out, and_8_out, and_9_out, dmr, and_10_out);
  D_FF D3 (.D(or_1_out), .C(clk), .Q(Q3), .nQ(D3_nq));
  D_FF D2 (.D(or_4_out), .C(clk), .Q(Q2), .nQ(D2_nq));
  D_FF D1 (.D(or_5_out), .C(clk), .Q(Q1), .nQ(D1_nq));
  D_FF D0 (.D(or_6_out), .C(clk), .Q(Q0), .nQ(D0_nq));
endmodule
